# Fritzing sketch ControlBox (saved by Fritzing 0.9.3b)
breadboards: 1

parts:
  Part1 = Arduino Mega ADK (Rev3)  # not connected
  S3 = Pushbutton [package="[THT]"]
  S4 = Pushbutton [package="[THT]"]
  S5 = Pushbutton [package="[THT]"]
  S6 = Pushbutton [package="[THT]"]
  R1 = Resistor [tolerance=±5% resistance=220 package=THT]
  WeMos_D1_Mini_Relay_Shield1 = WeMos D1 Mini Relay Shield  # not connected
  WeMos_D1_Mini_Relay_Shield_V1 = WeMos D1 Mini Relay Shield V2  # not connected

nets:
  N1: S3.Pin_1, S3.Pin_2
  N2: S3.Pin_3, S3.Pin_4
  N3: S4.Pin_1, S4.Pin_2
  N4: S4.Pin_3, S4.Pin_4
  N5: S5.Pin_1, S5.Pin_2
  N6: S5.Pin_3, S5.Pin_4
  N7: S6.Pin_1, S6.Pin_2
  N8: S6.Pin_3, S6.Pin_4, R1.Pin_0
